# Fritzing sketch 74HC595 (saved by Fritzing 0.8.7b)
breadboards: 1

parts:
  元件1 = Arduino Uno (Rev3)
  R1 = Resistor [tolerance=±5% resistance=220 package=THT]
  R2 = Resistor [tolerance=±5% resistance=220 package=THT]
  R3 = Resistor [tolerance=±5% resistance=220 package=THT]
  R4 = Resistor [tolerance=±5% resistance=220 package=THT]
  R5 = Resistor [tolerance=±5% resistance=220 package=THT]
  R6 = Resistor [tolerance=±5% resistance=220 package=THT]
  R7 = Resistor [tolerance=±5% resistance=220 package=THT]
  U1 = 74HC595 [package="DIP16 [THT]"]
  DI1 = 7-Segment LED Display [package=THT]
  R8 = Resistor [tolerance=±5% resistance=220 package=THT]

nets (from the schematic view):
  N1: 元件1.D8, U1.SH_CP
  N2: 元件1.D11_PWM/MOSI, U1.DS
  N3: 元件1.D12/MISO, U1.ST_CP
  GND: 元件1.GND, U1.GND, U1.OE, DI1.commAnode#2
  5V: 元件1.5V, U1.MR, U1.VCC
  N4: R1.Pin_0, U1.Q1
  N5: R1.Pin_1, DI1.cathodeG
  N6: R2.Pin_0, U1.Q3
  N7: R2.Pin_1, DI1.cathodeD
  N8: R3.Pin_0, DI1.cathodeC
  N9: R3.Pin_1, U1.Q5
  N10: R4.Pin_0, U1.Q2
  N11: R4.Pin_1, DI1.cathodeF
  N12: R5.Pin_0, DI1.cathodeDP
  N13: R5.Pin_1, U1.Q0
  N14: R6.Pin_0, DI1.cathodeA
  N15: R6.Pin_1, U1.Q7
  N16: R7.Pin_0, U1.Q4
  N17: R7.Pin_1, DI1.cathodeE
  N18: U1.Q6, R8.Pin_1
  N19: DI1.cathodeB, R8.Pin_0
